// Logisim project 16Bit_CPU_V2.circ as structural Verilog: 1 circuit, main circuit ManTest getrennt
module ManTest_getrennt (
  input  RST_IR,
  input  RST_IAR,
  input  HLT_PIPELINE,
  input  LD_PC,
  input  RST_PC,
  input  Pipeline_Reset,
  input  LD_BRBS,
  input  _2_TACT_INST,
  input  [1:0] A_SRC,
  input  LDA,
  input  RST_A,
  input  in_12,
  output Pipeline_DONE,
  output _2nd_TACT
);

  wire and_1_out, and_2_out, clock_1_out, not_1_out, not_2_out, not_3_out;
  wire [0:0] jmp_const;
  wire [4:0] opcode;
  wire [7:0] adder_1_out, adder_2_out, Akku_q, counter_1_q, IAR_q, multiplexer_1_out, multiplexer_2_out,
       ram_1_data, subtractor_1_out;
  wire [9:0] address;
  wire [15:0] rom_1_data;

  Clock clock_1 (.out(clock_1_out));
  not not_1 (not_1_out, HLT_PIPELINE);
  and and_1 (and_1_out, ~LD_PC, not_1_out);  // AND_Gate
  Multiplexer #(.width(8)) multiplexer_1 (
    .in0({address[6:0], jmp_const[0]}), .in1(subtractor_1_out), .out(multiplexer_1_out), .sel(LD_BRBS),
    .en(1'b1));
  Adder adder_1 (.a({2'b00, address[4:0], jmp_const[0]}), .b(counter_1_q), .out(adder_1_out));  // open: cin, cout
  Subtractor subtractor_1 (.a(adder_1_out), .b(8'h2), .out(subtractor_1_out));  // open: bin, bout
  // Probe on counter_1_q
  Counter counter_1 (
    .load(LD_PC), .D(multiplexer_1_out), .count(and_1_out), .Q(counter_1_q), .clk(clock_1_out), .clr(RST_PC));  // open: carry
  // Probe on counter_1_q
  Register IAR (.D(counter_1_q), .en(not_1_out), .Q(IAR_q), .clk(clock_1_out), .clr(RST_IAR));
  not not_2 (not_2_out, Pipeline_DONE);
  RAM #(.addrWidth(10), .bus("separate")) ram_1 (
    .addr(address), .din(Akku_q), .data(ram_1_data), .str(in_12), .sel(1'b1), .ld(1'b1), .clr(1'b0));  // open: clk
  S_R_Flip_Flop u_Pipeline_DONE (
    .S(not_2_out), .clk(clock_1_out), .R(1'b0), .Q(Pipeline_DONE), .reset(Pipeline_Reset));  // open: Qn, preset, en
  Multiplexer #(.select(2), .width(8)) multiplexer_2 (
    .in0(adder_2_out), .in1(address[9:2]), .in2(ram_1_data), .out(multiplexer_2_out), .sel(A_SRC), .en(1'b1));  // open: in3
  ROM #(.dataWidth(16)) rom_1 (.addr(IAR_q), .data(rom_1_data), .sel(1'b1));
  and and_2 (and_2_out, not_1_out, Pipeline_DONE);
  not not_3 (not_3_out, _2nd_TACT);
  Register Akku (.D(multiplexer_2_out), .en(LDA), .Q(Akku_q), .clk(clock_1_out), .clr(RST_A));
  Register #(.width(16)) register_1 (
    .D(rom_1_data), .en(and_2_out), .Q({opcode, address, jmp_const[0]}), .clk(clock_1_out), .clr(RST_IR));
  // Probe on opcode
  // Probe on opcode
  S_R_Flip_Flop u__2nd_tact (
    .S(_2_TACT_INST), .clk(clock_1_out), .R(not_3_out), .Q(_2nd_TACT));  // open: Qn, preset, reset, en
  Adder adder_2 (.a(Akku_q), .b(ram_1_data), .out(adder_2_out));  // open: cin, cout
  // Probe on address[9:2]
  // Probe on address[9:2]
  // Probe on address[9:2]
  // Probe on address
  // Probe on address
  // Probe on {address[6:0], jmp_const[0]}
  // Probe on {address[6:0], jmp_const[0]}
  // Probe on {address[6:0], jmp_const[0]}
  // Probe on address[9:5]
  // Probe on {address[4:0], jmp_const[0]}
  // Probe on {address[4:0], jmp_const[0]}
  // Probe on {address[4:0], jmp_const[0]}

  // Other names for the same wires on the sheet: offset[5:0] = {address[4:0], jmp_const[0]};
  //   jmp_const[7:1] = address[6:0]; ldi_const[7:0] = address[9:2]; psr_mask[4:0] = address[9:5]

  // Notes on the sheet:
  //   Programm Counter
  //   Enable Decoder Load
  //   Programmspeicher
  //   contents of rom_1 (hex, n*v repeats v):
  //   1d50 1b60 6a07 1878 1998 18f0 1878 1998 18f0 1cd0 1d50 1b60
  //   Opcode
  //   ALU
  //   Decoder Circuit
  //   Konstante
  //   OPCODE
  //   PSR
  //   Adresse
  //   JMP Konstante
  //   go into Decoder ROM
  //   PSR Mask
  //   Offset
endmodule
