// Logisim project 8-Bit CPU.circ as structural Verilog: 20 circuits, main circuit CPU
module CPU (
  input  Manuelles_Steuerwort,
  input  LF,
  input  CC,
  input  RR,
  input  WR,
  input  LM,
  input  LI,
  input  IP,
  input  EP,
  input  LP,
  input  LO,
  input  O4,
  input  O3,
  input  O2,
  input  O1,
  input  ET,
  input  LT,
  input  EA,
  input  LA,
  input  EB,
  input  LB,
  input  EC,
  input  LC,
  input  HLT
);

  wire ALU_c_out, ALU_is_neg, ALU_is_zero, AND_out, CLK_out, CLR_out, not_1_out, not_2_out, or_1_out;
  wire [2:0] n3_bit_flag_register_1_content_viewer, n3_bit_flag_register_1_out,
       \Zykluszähler_content_viewer , \Zykluszähler_out ;
  wire [7:0] A_Register_content_viewer_1, A_Register_content_viewer_2, A_Register_dir_out,
       Adress_Register_content_viewer_1, Adress_Register_content_viewer_2, Adress_Register_out,
       ALU_content_viewer_1, ALU_content_viewer_2, ALU_content_viewer_3, Ausgabe_Register_out,
       B_Register_content_viewer_1, B_Register_content_viewer_2, Befehlsregister_content_viewer_1,
       Befehlsregister_content_viewer_2, Befehlsregister_out, C_Register_content_viewer_1,
       C_Register_content_viewer_2, C_Register_out, n8_bit_pointer_2_1_content_viewer_1,
       n8_bit_pointer_2_1_content_viewer_1_2, n8_bit_pointer_2_1_content_viewer_1_3,
       TMP_Register_content_viewer_1, TMP_Register_content_viewer_2, TMP_Register_dir_out;
  wire [22:0] rom_1_data;
  wire [23:0] rom_2_data;

  or or_1 (or_1_out, CLR_out, CC);
  // Probe on Adress_Register_content_viewer_2
  // Probe on C_Register_content_viewer_1
  // Probe on Befehlsregister_content_viewer_2
  \_3_Bit_Zähler  \Zykluszähler  (
    .CLR(or_1_out), .CLK(AND_out), .OUT(\Zykluszähler_out ), .Content_Viewer(\Zykluszähler_content_viewer ));
  // Probe on \Zykluszähler_content_viewer 
  _8_Bit_Register Adress_Register (
    .CLK(AND_out), .Enable(1'b1), .Load(LM), .CLR(CLR_out), .D(C_Register_out), .OUT(Adress_Register_out),
    .Content_Viewer_1(Adress_Register_content_viewer_1), .Content_Viewer_2(Adress_Register_content_viewer_2));  // open: DIR_OUT
  _8_Bit_Register C_Register (
    .CLK(AND_out), .Enable(EC), .Load(LC), .CLR(CLR_out), .D(C_Register_out), .OUT(C_Register_out),
    .Content_Viewer_1(C_Register_content_viewer_1), .Content_Viewer_2(C_Register_content_viewer_2));  // open: DIR_OUT
  _8_Bit_Register Befehlsregister (
    .CLK(AND_out), .Enable(1'b1), .Load(LI), .CLR(CLR_out), .D(C_Register_out), .OUT(Befehlsregister_out),
    .Content_Viewer_1(Befehlsregister_content_viewer_1), .Content_Viewer_2(Befehlsregister_content_viewer_2));  // open: DIR_OUT
  _3_Bit_Flag_Register u_3_bit_flag_register_1 (
    .CLK(AND_out), .CLR(CLR_out), .Load(LF), .is_neg(ALU_is_neg), .is_zero(ALU_is_zero), .cout(ALU_c_out),
    .OUT(n3_bit_flag_register_1_out), .Content_Viewer(n3_bit_flag_register_1_content_viewer));
  // Probe on n3_bit_flag_register_1_content_viewer
  // Probe on Adress_Register_content_viewer_1
  _8_Bit_Pointer_2 u_8_bit_pointer_2_1 (
    .EP(EP), .LP(LP), .IP(IP), .CLK(AND_out), .CLR(CLR_out), .OUT(C_Register_out),
    .Content_Viewer_1(n8_bit_pointer_2_1_content_viewer_1),
    .Content_Viewer_1_2(n8_bit_pointer_2_1_content_viewer_1_2),
    .Content_Viewer_1_3(n8_bit_pointer_2_1_content_viewer_1_3), .D(C_Register_out));
  // Probe on n8_bit_pointer_2_1_content_viewer_1_3
  // Probe on n8_bit_pointer_2_1_content_viewer_1_2
  // Probe on n8_bit_pointer_2_1_content_viewer_1
  // Probe on C_Register_content_viewer_2
  // Probe on Befehlsregister_content_viewer_1
  RAM #(.bus("separate")) ram_1 (
    .addr(Adress_Register_out), .din(C_Register_out), .data(C_Register_out), .str(WR), .clk(AND_out), .ld(RR));  // open: sel, clr
  ROM #(.addrWidth(14), .dataWidth(23)) rom_1 (
    .addr({n3_bit_flag_register_1_out, Befehlsregister_out, \Zykluszähler_out }), .data(rom_1_data));  // open: sel
  // Probe on C_Register_out
  // Probe on C_Register_out
  // Probe on C_Register_out
  not not_1 (not_1_out, Manuelles_Steuerwort);
  assign {LF, CC, RR, WR, LM, LI, IP, EP, LP, LO, O4, O3, O2, O1, ET, LT, EA, LA, EB, LB, EC, LC, HLT} = not_1_out ? rom_1_data : 23'bz;  // Controlled_Buffer controlled_buffer_1
  // Probe on ALU_content_viewer_1
  _8_Bit_ALU ALU (
    .O3(O3), .O2(O2), .O1(O1), .C_out(ALU_c_out), .OUT(C_Register_out), .B(TMP_Register_dir_out),
    .A(A_Register_dir_out), .Content_Viewer_1(ALU_content_viewer_1), .Content_Viewer_2(ALU_content_viewer_2),
    .Content_Viewer_3(ALU_content_viewer_3), .is_zero(ALU_is_zero), .is_neg(ALU_is_neg), .O4(O4));
  // Probe on ALU_content_viewer_2
  // Probe on ALU_content_viewer_3
  _8_Bit_Register Ausgabe_Register (
    .CLK(AND_out), .Enable(1'b1), .Load(LO), .CLR(CLR_out), .D(C_Register_out), .OUT(Ausgabe_Register_out));  // open: Content_Viewer_1, Content_Viewer_2, DIR_OUT
  // Probe on A_Register_content_viewer_2
  // Probe on TMP_Register_content_viewer_1
  // Probe on B_Register_content_viewer_1
  _8_Bit_Register A_Register (
    .CLK(AND_out), .Enable(EA), .Load(LA), .CLR(CLR_out), .D(C_Register_out), .OUT(C_Register_out),
    .Content_Viewer_1(A_Register_content_viewer_1), .Content_Viewer_2(A_Register_content_viewer_2),
    .DIR_OUT(A_Register_dir_out));
  _8_Bit_Register TMP_Register (
    .CLK(AND_out), .Enable(ET), .Load(LT), .CLR(CLR_out), .D(C_Register_out), .OUT(C_Register_out),
    .Content_Viewer_1(TMP_Register_content_viewer_1), .Content_Viewer_2(TMP_Register_content_viewer_2),
    .DIR_OUT(TMP_Register_dir_out));
  _8_Bit_Register B_Register (
    .CLK(AND_out), .Enable(EB), .Load(LB), .CLR(CLR_out), .D(C_Register_out), .OUT(C_Register_out),
    .Content_Viewer_1(B_Register_content_viewer_1), .Content_Viewer_2(B_Register_content_viewer_2));  // open: DIR_OUT
  ROM #(.dataWidth(24)) rom_2 (.addr(Ausgabe_Register_out), .data(rom_2_data));  // open: sel
  // Probe on A_Register_content_viewer_1
  // Probe on TMP_Register_content_viewer_2
  // Probe on B_Register_content_viewer_2
  _7_Segment_Display u_7_segment_display_1 (
    .g(rom_2_data[19]), .f(rom_2_data[18]), .a(rom_2_data[17]), .b(rom_2_data[16]), .e(rom_2_data[20]),
    .d(rom_2_data[21]), .c(rom_2_data[22]), .dp(rom_2_data[23]));
  _7_Segment_Display u_7_segment_display_2 (
    .g(rom_2_data[11]), .f(rom_2_data[10]), .a(rom_2_data[9]), .b(rom_2_data[8]), .e(rom_2_data[12]),
    .d(rom_2_data[13]), .c(rom_2_data[14]), .dp(rom_2_data[15]));
  _7_Segment_Display u_7_segment_display_3 (
    .g(rom_2_data[3]), .f(rom_2_data[2]), .a(rom_2_data[1]), .b(rom_2_data[0]), .e(rom_2_data[4]),
    .d(rom_2_data[5]), .c(rom_2_data[6]), .dp(rom_2_data[7]));
  not not_2 (not_2_out, HLT);
  and AND (AND_out, not_2_out, CLK_out);
  Clock CLK (.out(CLK_out));
  Button CLR (.out(CLR_out));

  // Notes on the sheet:
  //   CLK
  //   CLR
  //   CLR
  //   CLK
  //   CLR
  //   CLK
  //   CLK
  //   CLR
  //   CLK
  //   CLR
  //   CC
  //   CLR
  //   CLK
  //   CC
  //   CLK
  //   CLR
  //   CLK
  //   CLR
  //   3
  //   LF
  //   8 Bit Bus
  //   8
  //   8
  //   8 Bit Bus
  //   CLR
  //   CLK
  //   8 Bit Bus
  //   8 Bit Bus
  //   CLK
  //   Steuersignale
  //   8 Bit Bus
  //   8
  //   14
  //   Flags
  //   3
  //   Flag Register
  //   Steuersignal
  //   RAM
  //   CLK
  //   Pointer
  //   CLR
  //   Steuersignal
  //   8 Bit Datenbus
  //   8 Bit Bus
  //   Steuersignale
  //   8 Bit Bus
  //   Steuersignale
  //   Steuerlogik
  //   23
  //   contents of rom_1 (hex, n*v repeats v):
  //   48000 130080 6*0 48000 130080 48000 110020 200000 0 0 0 48000 130080 48000 150000 100020 200000 0 0
  //   48000 130080 48000 110008 200000 0 0 0 48000 130080 48000 150000 100008 200000 0 0 48000 130080
  //   48000 110002 200000 0 0 0 48000 130080 48000 150000 100002 200000 0 0 48000 130080 48000 110080
  //   400220 200000 0 0 48000 130080 90 400220 200000 0 0 0 48000 130080 84 400220 200000 0 0 0 48000
  //   130080 48000 110080 400420 200000 0 0 48000 130080 90 400420 200000 0 0 0 48000 130080 84 400420
  //   200000 0 0 0 48000 130080 48000 110080 400620 200000 0 0 48000 130080 90 400620 200000 0 0 0 48000
  //   130080 84 400620 200000 0 0 0 48000 130080 48000 110080 400820 200000 0 0 48000 130080 90 400820
  //   200000 0 0 0 48000 130080 84 400820 200000 0 0 0 48000 130080 48000 110080 400c20 200000 0 0 48000
  //   130080 90 400c20 200000 0 0 0 48000 130080 84 400c20 200000 0 0 0 48000 130080 48000 110020 400a20
  //   200000 0 0 48000 130080 400a20 200000 4*0 48000 130080 30 400a20 200000 0 0 0 48000 130080 24 400a20
  //   200000 0 0 0 48000 130080 48000 150000 100020 400e20 200000 0 48000 130080 48000 110020 400e20
  //   200000 0 0 48000 130080 400e20 200000 4*0 48000 130080 30 400e20 200000 0 0 0 48000 130080 24 400e20
  //   200000 0 0 0 48000 130080 48000 150000 100020 401020 200000 0 48000 130080 48000 110020 401020
  //   200000 0 0 48000 130080 401020 200000 4*0 48000 130080 30 401020 200000 0 0 0 48000 130080 24 401020
  //   200000 0 0 0 48000 130080 401200 200000 4*0 48000 130080 2040 200000 4*0 48000 130080 2010 200000
  //   4*0 48000 130080 2004 200000 4*0 48000 130080 48000 150000 80040 200000 0 0 48000 130080 48000
  //   150000 80010 200000 0 0 48000 130080 48000 150000 80004 200000 0 0 48000 130080 48 200000 4*0 48000
  //   130080 42 200000 4*0 48000 130080 30 200000 4*0 48000 130080 12 200000 4*0 48000 130080 24 200000
  //   4*0 48000 130080 c 200000 4*0 48000 130080 48000 110080 400400 200000 0 0 48000 130080 90 400400
  //   200000 0 0 0 48000 130080 84 400400 200000 0 0 0 48000 130080 48000 104000 200000 0 0 0 48000 130080
  //   10000 200000 4*0 48000 130080 10000 200000 4*0 48000 130080 10000 200000 4*0 48000 130080 1 5*0
  //   48000 130080 40004 100020 200000 0 0 0 48000 130080 40004 100008 200000 0 0 0 48000 130080 40004
  //   100002 200000 0 0 0 48000 130080 40004 80040 200000 0 0 0 48000 130080 40004 80010 200000 0 0 0
  //   48000 130080 40004 80004 200000 0 0 0 48000 130080 6*0 48000 130080 6*0 48000 130080 6*0 48000
  //   130080 6*0 48000 130080 6*0 48000 130080 6*0 48000 130080 6*0 48000 130080 6*0 48000 130080 6*0
  //   48000 130080 6*0 48000 130080 6*0 48000 130080 6*0 48000 130080 6*0 48000 130080 6*0 48000 130080
  //   6*0 48000 130080 6*0 48000 130080 6*0 48000 130080 6*0 48000 130080 6*0 48000 130080 6*0 48000
  //   130080 6*0 48000 130080 6*0 48000 130080 6*0 48000 130080 6*0 48000 130080 6*0 48000 130080 6*0
  //   48000 130080 6*0 48000 130080 6*0 48000 130080 6*0 48000 130080 6*0 48000 130080 6*0 48000 130080
  //   6*0 48000 130080 6*0 48000 130080 6*0 48000 130080 6*0 48000 130080 6*0 48000 130080 6*0 48000
  //   130080 6*0 48000 130080 6*0 48000 130080 6*0 48000 130080 6*0 48000 130080 6*0 48000 130080 6*0
  //   48000 130080 6*0 48000 130080 6*0 48000 130080 6*0 48000 130080 6*0 48000 130080 6*0 48000 130080
  //   6*0 48000 130080 6*0 48000 130080 6*0 48000 130080 6*0 48000 130080 6*0 48000 130080 6*0 48000
  //   130080 6*0 48000 130080 6*0 48000 130080 6*0 48000 130080 6*0 48000 130080 6*0 48000 130080 6*0
  //   48000 130080 6*0 48000 130080 6*0 48000 130080 6*0 48000 130080 6*0 48000 130080 6*0 48000 130080
  //   6*0 48000 130080 6*0 48000 130080 6*0 48000 130080 6*0 48000 130080 6*0 48000 130080 6*0 48000
  //   130080 6*0 48000 130080 6*0 48000 130080 6*0 48000 130080 6*0 48000 130080 6*0 48000 130080 6*0
  //   48000 130080 6*0 48000 130080 6*0 48000 130080 6*0 48000 130080 6*0 48000 130080 6*0 48000 130080
  //   6*0 48000 130080 6*0 48000 130080 6*0 48000 130080 6*0 48000 130080 6*0 48000 130080 6*0 48000
  //   130080 6*0 48000 130080 6*0 48000 130080 6*0 48000 130080 6*0 48000 130080 6*0 48000 130080 6*0
  //   48000 130080 6*0 48000 130080 6*0 48000 130080 6*0 48000 130080 6*0 48000 130080 6*0 48000 130080
  //   6*0 48000 130080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
  //   Flags
  //   8 Bit Bus
  //   8 Bit Bus
  //   8 Bit Bus
  //   Steuerwort
  //   23
  //   Steuersignal
  //   8 Bit Bus
  //   CLR
  //   CLK
  //   8 Bit Bus
  //   8 Bit Bus
  //   8
  //   CLR
  //   8
  //   8
  //   Flags
  //   8 Bit Bus
  //   22 Bit Steuerwort
  //   CLK
  //   8 Bit Bus
  //   8
  //   8 Bit Bus
  //   A Operand
  //   B Operand
  //   8
  //   8 Bit Bus
  //   Steuersignale
  //   24
  //   contents of rom_2 (hex, n*v repeats v):
  //   77 41 3b 6b 4d 6e 7e 43 7f 6f 4177 4141 413b 416b 414d 416e 417e 4143 417f 416f 3b77 3b41 3b3b 3b6b
  //   3b4d 3b6e 3b7e 3b43 3b7f 3b6f 6b77 6b41 6b3b 6b6b 6b4d 6b6e 6b7e 6b43 6b7f 6b6f 4d77 4d41 4d3b 4d6b
  //   4d4d 4d6e 4d7e 4d43 4d7f 4d6f 6e77 6e41 6e3b 6e6b 6e4d 6e6e 6e7e 6e43 6e7f 6e6f 7e77 7e41 7e3b 7e6b
  //   7e4d 7e6e 7e7e 7e43 7e7f 7e6f 4377 4341 433b 436b 434d 436e 437e 4343 437f 436f 7f77 7f41 7f3b 7f6b
  //   7f4d 7f6e 7f7e 7f43 7f7f 7f6f 6f77 6f41 6f3b 6f6b 6f4d 6f6e 6f7e 6f43 6f7f 6f6f 417777 417741 41773b
  //   41776b 41774d 41776e 41777e 417743 41777f 41776f 414177 414141 41413b 41416b 41414d 41416e 41417e
  //   414143 41417f 41416f 413b77 413b41 413b3b 413b6b 413b4d 413b6e 413b7e 413b43 413b7f 413b6f 416b77
  //   416b41 416b3b 416b6b 416b4d 416b6e 416b7e 416b43 416b7f 416b6f 414d77 414d41 414d3b 414d6b 414d4d
  //   414d6e 414d7e 414d43 414d7f 414d6f 416e77 416e41 416e3b 416e6b 416e4d 416e6e 416e7e 416e43 416e7f
  //   416e6f 417e77 417e41 417e3b 417e6b 417e4d 417e6e 417e7e 417e43 417e7f 417e6f 414377 414341 41433b
  //   41436b 41434d 41436e 41437e 414343 41437f 41436f 417f77 417f41 417f3b 417f6b 417f4d 417f6e 417f7e
  //   417f43 417f7f 417f6f 416f77 416f41 416f3b 416f6b 416f4d 416f6e 416f7e 416f43 416f7f 416f6f 3b7777
  //   3b7741 3b773b 3b776b 3b774d 3b776e 3b777e 3b7743 3b777f 3b776f 3b4177 3b4141 3b413b 3b416b 3b414d
  //   3b416e 3b417e 3b4143 3b417f 3b416f 3b3b77 3b3b41 3b3b3b 3b3b6b 3b3b4d 3b3b6e 3b3b7e 3b3b43 3b3b7f
  //   3b3b6f 3b6b77 3b6b41 3b6b3b 3b6b6b 3b6b4d 3b6b6e 3b6b7e 3b6b43 3b6b7f 3b6b6f 3b4d77 3b4d41 3b4d3b
  //   3b4d6b 3b4d4d 3b4d6e 3b4d7e 3b4d43 3b4d7f 3b4d6f 3b6e77 3b6e41 3b6e3b 3b6e6b 3b6e4d 3b6e6e
  //   Steuersignale
  //   Steuersignale
  //   8 Bit Bus
  //   CLR
  //   CLK
  //   Steuersignale
  //   8 Bit Bus
  //   CLR
  //   CLK
  //   Steuersignale
  //   Steuersignale
  //   Steuersignale
  //   CLK
  //   CLK
  //   CLK
  //   CLR
  //   CLR
  //   Flags
  //   CLR
  //   HLT Logik
  //   CLK
  //   CLK
  //   Flags
  //   Flags
endmodule

module Testplatine (
  input  in_1,
  input  [15:0] in_2,
  input  in_3,
  input  in_4,
  input  [15:0] in_5,
  input  in_6,
  input  [3:0] in_7,
  input  ENABLE,
  input  LOAD,
  input  CLK,
  input  CLR,
  input  [15:0] DIN,
  input  [15:0] B,
  output [15:0] out_14,
  output [15:0] out_15,
  output CY,
  output OV
);

  wire [15:0] multiplexer_1_out, n16_bit_alu_1_content_viewer_1, n16_bit_alu_1_content_viewer_2,
       n16_bit_alu_1_content_viewer_3, n16_bit_alu_1_content_viewer_4, n16_bit_pointer_1_content_viewer_1,
       n16_bit_pointer_1_content_viewer_1_2, n16_bit_pointer_1_content_viewer_1_3,
       n16_bit_register_1_content_viewer_1, n16_bit_register_1_content_viewer_2,
       n16_bit_register_1_content_viewer_3, n16_bit_register_1_dir_out;

  // Probe on n16_bit_pointer_1_content_viewer_1_3
  _16_Bit_Pointer u_16_bit_pointer_1 (
    .Content_Viewer_1(n16_bit_pointer_1_content_viewer_1),
    .Content_Viewer_1_2(n16_bit_pointer_1_content_viewer_1_2),
    .Content_Viewer_1_3(n16_bit_pointer_1_content_viewer_1_3));  // open: EP, LP, IP, CLK, CLR, OUT, D
  _16_Bit_IO_Controller u_16_bit_io_controller_1 (
    .CPU_OUT(out_14), .CPU_IN(in_2), .L_IOMAR(in_1), .W_IO(in_3), .R_IO(in_4));  // open: D_IN, D_OUT, CS_1, CS_2, CS_3, CS_4, CS_5, CS_6, CS_7, CS_0, Address, DR_1, DR_2, DR_3, DR_4, DR_5, DR_6, DR_7, DR_0, IE, IFG, IR, CLK
  // Probe on n16_bit_pointer_1_content_viewer_1_2
  // Probe on n16_bit_pointer_1_content_viewer_1
  _16_Bit_Register u_16_bit_register_1 (
    .CLK(CLK), .CLR(CLR), .Enable(ENABLE), .Load(LOAD), .D(DIN), .DIR_OUT(n16_bit_register_1_dir_out),
    .Content_Viewer_1(n16_bit_register_1_content_viewer_1),
    .Content_Viewer_2(n16_bit_register_1_content_viewer_2),
    .Content_Viewer_3(n16_bit_register_1_content_viewer_3));  // open: OUT
  // Probe on n16_bit_register_1_content_viewer_1
  // Probe on n16_bit_register_1_content_viewer_2
  // Probe on n16_bit_register_1_content_viewer_3
  // Probe on n16_bit_alu_1_content_viewer_1
  Multiplexer #(.width(16), .enable("false")) multiplexer_1 (
    .in0(n16_bit_register_1_dir_out), .in1(in_5), .out(multiplexer_1_out), .sel(in_6));
  _16_Bit_ALU u_16_bit_alu_1 (
    .O4(in_7[3]), .O3(in_7[2]), .O2(in_7[1]), .O1(in_7[0]), .OUT(out_15),
    .CONTENT_VIEWER_1(n16_bit_alu_1_content_viewer_1), .CONTENT_VIEWER_2(n16_bit_alu_1_content_viewer_2),
    .CONTENT_VIEWER_3(n16_bit_alu_1_content_viewer_3), .B1(B), .A1(multiplexer_1_out), .COUT(CY),
    .CONTENT_VIEWER_4(n16_bit_alu_1_content_viewer_4), .OV(OV));  // open: NEG, ZERO
  // Probe on n16_bit_alu_1_content_viewer_2
  // Probe on n16_bit_alu_1_content_viewer_3
  // Probe on n16_bit_alu_1_content_viewer_4

  // Notes on the sheet:
  //   0000 None
  //   0001 ADD
  //   0010 SUB
  //   0011 AND
  //   0100 OR
  //   0101 NOT
  //   0110 XOR
  //   0111 DEC
  //   1000 INC
  //   1001 AOUT
  //   1010 SHIFTL
  //   1011 SHIFTR
endmodule

module _1_Bit_Register (
  input  CLR,
  input  CLK,
  input  Load,
  input  D1,
  output OUT
);

  wire AND_2_out, AND_out, NOR_2_out, not_1_out, OR_out;

  not not_1 (not_1_out, D1);
  and AND (AND_out, not_1_out, Load, CLK);
  and AND_2 (AND_2_out, CLK, Load, D1);
  or OR (OR_out, CLR, AND_out);
  nor NOR (OUT, OR_out, NOR_2_out);
  nor NOR_2 (NOR_2_out, OUT, AND_2_out);
endmodule

module _8_Bit_Register (
  input  CLK,
  input  CLR,
  input  Enable,
  input  Load,
  input  [7:0] D,
  output [7:0] OUT,
  output [7:0] DIR_OUT,
  output [7:0] Content_Viewer_1,
  output [7:0] Content_Viewer_2
);

  wire and_1_out, not_1_out, not_2_out, not_3_out;

  not not_1 (not_1_out, CLK);
  Pull_Resistor pull_resistor_1 (.node(Enable));
  Pull_Resistor pull_resistor_2 (.node(Load));
  not not_2 (not_2_out, not_1_out);
  not not_3 (not_3_out, not_2_out);
  and and_1 (and_1_out, CLK, not_3_out);
  _1_Bit_Register u_1_bit_register_1 (.D1(D[0]), .OUT(Content_Viewer_1[0]), .CLK(and_1_out), .Load(Load), .CLR(CLR));
  _1_Bit_Register u_1_bit_register_2 (.D1(D[1]), .OUT(Content_Viewer_1[1]), .CLK(and_1_out), .Load(Load), .CLR(CLR));
  _1_Bit_Register u_1_bit_register_3 (.D1(D[2]), .OUT(Content_Viewer_1[2]), .CLK(and_1_out), .Load(Load), .CLR(CLR));
  _1_Bit_Register u_1_bit_register_4 (.D1(D[3]), .OUT(Content_Viewer_1[3]), .CLK(and_1_out), .Load(Load), .CLR(CLR));
  _1_Bit_Register u_1_bit_register_5 (.D1(D[4]), .OUT(Content_Viewer_1[4]), .CLK(and_1_out), .Load(Load), .CLR(CLR));
  _1_Bit_Register u_1_bit_register_6 (.D1(D[5]), .OUT(Content_Viewer_1[5]), .CLK(and_1_out), .Load(Load), .CLR(CLR));
  _1_Bit_Register u_1_bit_register_7 (.D1(D[6]), .OUT(Content_Viewer_1[6]), .CLK(and_1_out), .Load(Load), .CLR(CLR));
  _1_Bit_Register u_1_bit_register_8 (.D1(D[7]), .OUT(Content_Viewer_1[7]), .CLK(and_1_out), .Load(Load), .CLR(CLR));
  assign OUT[0] = Enable ? Content_Viewer_1[0] : 1'bz;  // Controlled_Buffer controlled_buffer_1
  assign OUT[1] = Enable ? Content_Viewer_1[1] : 1'bz;  // Controlled_Buffer controlled_buffer_2
  assign OUT[2] = Enable ? Content_Viewer_1[2] : 1'bz;  // Controlled_Buffer controlled_buffer_3
  assign OUT[3] = Enable ? Content_Viewer_1[3] : 1'bz;  // Controlled_Buffer controlled_buffer_4
  assign OUT[4] = Enable ? Content_Viewer_1[4] : 1'bz;  // Controlled_Buffer controlled_buffer_5
  assign OUT[5] = Enable ? Content_Viewer_1[5] : 1'bz;  // Controlled_Buffer controlled_buffer_6
  assign OUT[6] = Enable ? Content_Viewer_1[6] : 1'bz;  // Controlled_Buffer controlled_buffer_7
  assign OUT[7] = Enable ? Content_Viewer_1[7] : 1'bz;  // Controlled_Buffer controlled_buffer_8

  assign Content_Viewer_2 = Content_Viewer_1;
  assign DIR_OUT = Content_Viewer_1;
endmodule

module _16_Bit_Register (
  input  CLK,
  input  CLR,
  input  Enable,
  input  Load,
  input  [15:0] D,
  output [15:0] DIR_OUT,
  output [15:0] OUT,
  output [15:0] Content_Viewer_1,
  output [15:0] Content_Viewer_2,
  output [15:0] Content_Viewer_3
);

  wire and_1_out, not_1_out, not_2_out, not_3_out;

  not not_1 (not_1_out, CLK);
  not not_2 (not_2_out, not_1_out);
  Pull_Resistor pull_resistor_1 (.node(Enable));
  Pull_Resistor pull_resistor_2 (.node(Load));
  and and_1 (and_1_out, CLK, not_3_out);
  not not_3 (not_3_out, not_2_out);
  _1_Bit_Register u_1_bit_register_1 (.D1(D[0]), .OUT(Content_Viewer_1[0]), .CLK(and_1_out), .Load(Load), .CLR(CLR));
  _1_Bit_Register u_1_bit_register_2 (.D1(D[1]), .OUT(Content_Viewer_1[1]), .CLK(and_1_out), .Load(Load), .CLR(CLR));
  _1_Bit_Register u_1_bit_register_3 (.D1(D[2]), .OUT(Content_Viewer_1[2]), .CLK(and_1_out), .Load(Load), .CLR(CLR));
  _1_Bit_Register u_1_bit_register_4 (.D1(D[3]), .OUT(Content_Viewer_1[3]), .CLK(and_1_out), .Load(Load), .CLR(CLR));
  _1_Bit_Register u_1_bit_register_5 (.D1(D[4]), .OUT(Content_Viewer_1[4]), .CLK(and_1_out), .Load(Load), .CLR(CLR));
  _1_Bit_Register u_1_bit_register_6 (.D1(D[5]), .OUT(Content_Viewer_1[5]), .CLK(and_1_out), .Load(Load), .CLR(CLR));
  _1_Bit_Register u_1_bit_register_7 (.D1(D[6]), .OUT(Content_Viewer_1[6]), .CLK(and_1_out), .Load(Load), .CLR(CLR));
  _1_Bit_Register u_1_bit_register_8 (.D1(D[7]), .OUT(Content_Viewer_1[7]), .CLK(and_1_out), .Load(Load), .CLR(CLR));
  _1_Bit_Register u_1_bit_register_9 (.D1(D[8]), .OUT(Content_Viewer_1[8]), .CLK(and_1_out), .Load(Load), .CLR(CLR));
  _1_Bit_Register u_1_bit_register_10 (.D1(D[9]), .OUT(Content_Viewer_1[9]), .CLK(and_1_out), .Load(Load), .CLR(CLR));
  _1_Bit_Register u_1_bit_register_11 (.D1(D[10]), .OUT(Content_Viewer_1[10]), .CLK(and_1_out), .Load(Load), .CLR(CLR));
  _1_Bit_Register u_1_bit_register_12 (.D1(D[11]), .OUT(Content_Viewer_1[11]), .CLK(and_1_out), .Load(Load), .CLR(CLR));
  _1_Bit_Register u_1_bit_register_13 (.D1(D[12]), .OUT(Content_Viewer_1[12]), .CLK(and_1_out), .Load(Load), .CLR(CLR));
  _1_Bit_Register u_1_bit_register_14 (.D1(D[13]), .OUT(Content_Viewer_1[13]), .CLK(and_1_out), .Load(Load), .CLR(CLR));
  _1_Bit_Register u_1_bit_register_15 (.D1(D[14]), .OUT(Content_Viewer_1[14]), .CLK(and_1_out), .Load(Load), .CLR(CLR));
  _1_Bit_Register u_1_bit_register_16 (.D1(D[15]), .OUT(Content_Viewer_1[15]), .CLK(and_1_out), .Load(Load), .CLR(CLR));
  assign OUT[0] = Enable ? Content_Viewer_1[0] : 1'bz;  // Controlled_Buffer controlled_buffer_1
  assign OUT[1] = Enable ? Content_Viewer_1[1] : 1'bz;  // Controlled_Buffer controlled_buffer_2
  assign OUT[2] = Enable ? Content_Viewer_1[2] : 1'bz;  // Controlled_Buffer controlled_buffer_3
  assign OUT[3] = Enable ? Content_Viewer_1[3] : 1'bz;  // Controlled_Buffer controlled_buffer_4
  assign OUT[4] = Enable ? Content_Viewer_1[4] : 1'bz;  // Controlled_Buffer controlled_buffer_5
  assign OUT[5] = Enable ? Content_Viewer_1[5] : 1'bz;  // Controlled_Buffer controlled_buffer_6
  assign OUT[6] = Enable ? Content_Viewer_1[6] : 1'bz;  // Controlled_Buffer controlled_buffer_7
  assign OUT[7] = Enable ? Content_Viewer_1[7] : 1'bz;  // Controlled_Buffer controlled_buffer_8
  assign OUT[8] = Enable ? Content_Viewer_1[8] : 1'bz;  // Controlled_Buffer controlled_buffer_9
  assign OUT[9] = Enable ? Content_Viewer_1[9] : 1'bz;  // Controlled_Buffer controlled_buffer_10
  assign OUT[10] = Enable ? Content_Viewer_1[10] : 1'bz;  // Controlled_Buffer controlled_buffer_11
  assign OUT[11] = Enable ? Content_Viewer_1[11] : 1'bz;  // Controlled_Buffer controlled_buffer_12
  assign OUT[12] = Enable ? Content_Viewer_1[12] : 1'bz;  // Controlled_Buffer controlled_buffer_13
  assign OUT[13] = Enable ? Content_Viewer_1[13] : 1'bz;  // Controlled_Buffer controlled_buffer_14
  assign OUT[14] = Enable ? Content_Viewer_1[14] : 1'bz;  // Controlled_Buffer controlled_buffer_15
  assign OUT[15] = Enable ? Content_Viewer_1[15] : 1'bz;  // Controlled_Buffer controlled_buffer_16

  assign Content_Viewer_2 = Content_Viewer_1;
  assign Content_Viewer_3 = Content_Viewer_1;
  assign DIR_OUT = Content_Viewer_1;
endmodule

module _3_Bit_Flag_Register (
  input  CLK,
  input  CLR,
  input  Load,
  input  is_neg,
  input  is_zero,
  input  cout,
  output [2:0] OUT,
  output [2:0] Content_Viewer
);

  wire and_1_out, not_1_out, not_2_out, not_3_out;

  not not_1 (not_1_out, CLK);
  not not_2 (not_2_out, not_1_out);
  Pull_Resistor pull_resistor_1 (.node(Load));
  and and_1 (and_1_out, CLK, not_3_out);
  not not_3 (not_3_out, not_2_out);
  _1_Bit_Register u_1_bit_register_1 (.D1(is_neg), .OUT(Content_Viewer[0]), .CLK(and_1_out), .Load(Load), .CLR(CLR));
  _1_Bit_Register u_1_bit_register_2 (.D1(is_zero), .OUT(Content_Viewer[1]), .CLK(and_1_out), .Load(Load), .CLR(CLR));
  _1_Bit_Register u_1_bit_register_3 (.D1(cout), .OUT(Content_Viewer[2]), .CLK(and_1_out), .Load(Load), .CLR(CLR));

  assign OUT = Content_Viewer;
endmodule

// 1Bit\nAdder
module _1_Bit_Volladdierer (
  input  Sub,
  input  C_in,
  input  A,
  input  B,
  output S,
  output C_out
);

  wire AND_2_out, AND_out, XOR_2_out, XOR_out;

  xor XOR (XOR_out, Sub, B);
  xor XOR_2 (XOR_2_out, A, XOR_out);
  and AND (AND_out, A, XOR_out);
  xor XOR_3 (S, C_in, XOR_2_out);
  and AND_2 (AND_2_out, C_in, XOR_2_out);
  or OR (C_out, AND_2_out, AND_out);
endmodule

module _8_Bit_Volladdierer (
  input  Sub,
  input  [7:0] A,
  input  [7:0] B,
  output [7:0] SUM,
  output C_out
);

  wire n1_bit_volladdierer_1_c_out, n1_bit_volladdierer_2_c_out, n1_bit_volladdierer_3_c_out,
       n1_bit_volladdierer_4_c_out, n1_bit_volladdierer_5_c_out, n1_bit_volladdierer_6_c_out,
       n1_bit_volladdierer_7_c_out;

  _1_Bit_Volladdierer u_1_bit_volladdierer_1 (
    .C_in(Sub), .A(A[0]), .B(B[0]), .S(SUM[0]), .C_out(n1_bit_volladdierer_1_c_out), .Sub(Sub));
  _1_Bit_Volladdierer u_1_bit_volladdierer_2 (
    .C_in(n1_bit_volladdierer_1_c_out), .A(A[1]), .B(B[1]), .S(SUM[1]), .C_out(n1_bit_volladdierer_2_c_out),
    .Sub(Sub));
  _1_Bit_Volladdierer u_1_bit_volladdierer_3 (
    .C_in(n1_bit_volladdierer_2_c_out), .A(A[2]), .B(B[2]), .S(SUM[2]), .C_out(n1_bit_volladdierer_3_c_out),
    .Sub(Sub));
  _1_Bit_Volladdierer u_1_bit_volladdierer_4 (
    .C_in(n1_bit_volladdierer_3_c_out), .A(A[3]), .B(B[3]), .S(SUM[3]), .C_out(n1_bit_volladdierer_4_c_out),
    .Sub(Sub));
  _1_Bit_Volladdierer u_1_bit_volladdierer_5 (
    .C_in(n1_bit_volladdierer_4_c_out), .A(A[4]), .B(B[4]), .S(SUM[4]), .C_out(n1_bit_volladdierer_5_c_out),
    .Sub(Sub));
  _1_Bit_Volladdierer u_1_bit_volladdierer_6 (
    .C_in(n1_bit_volladdierer_5_c_out), .A(A[5]), .B(B[5]), .S(SUM[5]), .C_out(n1_bit_volladdierer_6_c_out),
    .Sub(Sub));
  _1_Bit_Volladdierer u_1_bit_volladdierer_7 (
    .C_in(n1_bit_volladdierer_6_c_out), .A(A[6]), .B(B[6]), .S(SUM[6]), .C_out(n1_bit_volladdierer_7_c_out),
    .Sub(Sub));
  _1_Bit_Volladdierer u_1_bit_volladdierer_8 (
    .C_in(n1_bit_volladdierer_7_c_out), .A(A[7]), .B(B[7]), .S(SUM[7]), .C_out(C_out), .Sub(Sub));
endmodule

module _1_Bit_ALU (
  input  Sub,
  input  C_in,
  input  A1,
  input  B1,
  output NOT,
  output AND,
  output OR,
  output XOR,
  output SUM,
  output C_out
);

  not not_1 (NOT, A1);
  and and_1 (AND, A1, B1);
  or or_1 (OR, A1, B1);
  xor xor_1 (XOR, A1, B1);
  _1_Bit_Volladdierer u_1_bit_volladdierer_1 (.C_in(C_in), .A(A1), .B(B1), .S(SUM), .C_out(C_out), .Sub(Sub));
endmodule

// Multiplexer
module _1_Bit_Multiplexer (
  input  O4,
  input  O3,
  input  O2,
  input  O1,
  input  NOT,
  input  AND,
  input  OR,
  input  XOR,
  input  SUM,
  output out_10
);

  wire AND_2_out, AND_3_out, AND_4_out, AND_5_out, AND_6_out, AND_7_out, AND_8_out, AND_9_out, AND_out,
       not_1_out, not_2_out, not_3_out, not_4_out;

  not not_1 (not_1_out, O4);
  not not_2 (not_2_out, O3);
  not not_3 (not_3_out, O2);
  not not_4 (not_4_out, O1);
  and u_AND (AND_out, not_1_out, O3, not_3_out, O1, NOT);
  and AND_2 (AND_2_out, not_1_out, not_2_out, O2, O1, AND);
  and AND_3 (AND_3_out, not_1_out, O3, not_3_out, not_4_out, OR);
  and AND_4 (AND_4_out, not_1_out, O3, O2, not_4_out, XOR);
  and AND_5 (AND_5_out, not_1_out, not_2_out, not_3_out, O1, SUM);
  and AND_6 (AND_6_out, not_1_out, not_2_out, O2, not_4_out, SUM);
  and AND_7 (AND_7_out, not_1_out, O3, O2, O1, SUM);
  and AND_8 (AND_8_out, O4, not_2_out, not_3_out, not_4_out, SUM);
  and AND_9 (AND_9_out, O4, not_2_out, not_3_out, O1, SUM);
  or u_OR (out_10, AND_out, AND_2_out, AND_3_out, AND_4_out, AND_5_out, AND_6_out, AND_7_out, AND_8_out, AND_9_out);
endmodule

module _8_Bit_ALU (
  input  O4,
  input  O3,
  input  O2,
  input  O1,
  input  [7:0] A,
  input  [7:0] B,
  output [7:0] Content_Viewer_1,
  output [7:0] OUT,
  output [7:0] Content_Viewer_2,
  output [7:0] Content_Viewer_3,
  output C_out,
  output is_zero,
  output is_neg
);

  wire and_1_out, and_2_out, and_3_out, and_4_out, and_5_out, and_6_out, and_7_out, and_8_out, AOUT_out,
       DEC_out, INC_out, n1_bit_alu_1_and, n1_bit_alu_1_c_out, n1_bit_alu_1_not, n1_bit_alu_1_or,
       n1_bit_alu_1_sum, n1_bit_alu_1_xor, n1_bit_alu_2_and, n1_bit_alu_2_c_out, n1_bit_alu_2_not,
       n1_bit_alu_2_or, n1_bit_alu_2_sum, n1_bit_alu_2_xor, n1_bit_alu_3_and, n1_bit_alu_3_c_out,
       n1_bit_alu_3_not, n1_bit_alu_3_or, n1_bit_alu_3_sum, n1_bit_alu_3_xor, n1_bit_alu_4_and,
       n1_bit_alu_4_c_out, n1_bit_alu_4_not, n1_bit_alu_4_or, n1_bit_alu_4_sum, n1_bit_alu_4_xor,
       n1_bit_alu_5_and, n1_bit_alu_5_c_out, n1_bit_alu_5_not, n1_bit_alu_5_or, n1_bit_alu_5_sum,
       n1_bit_alu_5_xor, n1_bit_alu_6_and, n1_bit_alu_6_c_out, n1_bit_alu_6_not, n1_bit_alu_6_or,
       n1_bit_alu_6_sum, n1_bit_alu_6_xor, n1_bit_alu_7_and, n1_bit_alu_7_c_out, n1_bit_alu_7_not,
       n1_bit_alu_7_or, n1_bit_alu_7_sum, n1_bit_alu_7_xor, n1_bit_alu_8_and, n1_bit_alu_8_not,
       n1_bit_alu_8_or, n1_bit_alu_8_sum, n1_bit_alu_8_xor, not_1_out, not_2_out, not_3_out, not_4_out,
       not_5_out, not_6_out, not_7_out, not_8_out, not_9_out, not_10_out, or_1_out, or_2_out, or_3_out,
       OR_4_out, or_5_out, SUB_out;

  not not_1 (not_1_out, O3);
  not not_2 (not_2_out, O1);
  not not_3 (not_3_out, O4);
  and SUB (SUB_out, not_3_out, not_1_out, O2, not_2_out);
  or or_1 (or_1_out, AOUT_out, INC_out, DEC_out);
  not not_4 (not_4_out, or_1_out);
  not not_5 (not_5_out, O3);
  not not_6 (not_6_out, O4);
  and DEC (DEC_out, not_6_out, O3, O2, O1);
  not not_7 (not_7_out, O2);
  not not_8 (not_8_out, O2);
  not not_9 (not_9_out, O1);
  not not_10 (not_10_out, O3);
  and AOUT (AOUT_out, O4, not_10_out, not_7_out, O1);
  and INC (INC_out, O4, not_5_out, not_8_out, not_9_out);
  or or_2 (or_2_out, DEC_out, SUB_out);
  or or_3 (or_3_out, INC_out, SUB_out);
  Pull_Resistor pull_resistor_1 (.node(O1));
  Pull_Resistor pull_resistor_2 (.node(O2));
  Pull_Resistor pull_resistor_3 (.node(O4));
  Pull_Resistor pull_resistor_4 (.node(O3));
  _1_Bit_ALU u_1_bit_alu_1 (
    .A1(A[0]), .B1(and_1_out), .Sub(or_2_out), .C_in(or_3_out), .SUM(n1_bit_alu_1_sum),
    .XOR(n1_bit_alu_1_xor), .OR(n1_bit_alu_1_or), .AND(n1_bit_alu_1_and), .NOT(n1_bit_alu_1_not),
    .C_out(n1_bit_alu_1_c_out));
  and and_1 (and_1_out, not_4_out, B[0]);
  _1_Bit_ALU u_1_bit_alu_2 (
    .A1(A[1]), .B1(and_2_out), .Sub(or_2_out), .C_in(n1_bit_alu_1_c_out), .SUM(n1_bit_alu_2_sum),
    .XOR(n1_bit_alu_2_xor), .OR(n1_bit_alu_2_or), .AND(n1_bit_alu_2_and), .NOT(n1_bit_alu_2_not),
    .C_out(n1_bit_alu_2_c_out));
  and and_2 (and_2_out, not_4_out, B[1]);
  _1_Bit_ALU u_1_bit_alu_3 (
    .A1(A[2]), .B1(and_3_out), .Sub(or_2_out), .C_in(n1_bit_alu_2_c_out), .SUM(n1_bit_alu_3_sum),
    .XOR(n1_bit_alu_3_xor), .OR(n1_bit_alu_3_or), .AND(n1_bit_alu_3_and), .NOT(n1_bit_alu_3_not),
    .C_out(n1_bit_alu_3_c_out));
  and and_3 (and_3_out, not_4_out, B[2]);
  _1_Bit_ALU u_1_bit_alu_4 (
    .A1(A[3]), .B1(and_4_out), .Sub(or_2_out), .C_in(n1_bit_alu_3_c_out), .SUM(n1_bit_alu_4_sum),
    .XOR(n1_bit_alu_4_xor), .OR(n1_bit_alu_4_or), .AND(n1_bit_alu_4_and), .NOT(n1_bit_alu_4_not),
    .C_out(n1_bit_alu_4_c_out));
  and and_4 (and_4_out, not_4_out, B[3]);
  _1_Bit_ALU u_1_bit_alu_5 (
    .A1(A[4]), .B1(and_5_out), .Sub(or_2_out), .C_in(n1_bit_alu_4_c_out), .SUM(n1_bit_alu_5_sum),
    .XOR(n1_bit_alu_5_xor), .OR(n1_bit_alu_5_or), .AND(n1_bit_alu_5_and), .NOT(n1_bit_alu_5_not),
    .C_out(n1_bit_alu_5_c_out));
  and and_5 (and_5_out, not_4_out, B[4]);
  _1_Bit_ALU u_1_bit_alu_6 (
    .A1(A[5]), .B1(and_6_out), .Sub(or_2_out), .C_in(n1_bit_alu_5_c_out), .SUM(n1_bit_alu_6_sum),
    .XOR(n1_bit_alu_6_xor), .OR(n1_bit_alu_6_or), .AND(n1_bit_alu_6_and), .NOT(n1_bit_alu_6_not),
    .C_out(n1_bit_alu_6_c_out));
  and and_6 (and_6_out, not_4_out, B[5]);
  _1_Bit_ALU u_1_bit_alu_7 (
    .A1(A[6]), .B1(and_7_out), .Sub(or_2_out), .C_in(n1_bit_alu_6_c_out), .SUM(n1_bit_alu_7_sum),
    .XOR(n1_bit_alu_7_xor), .OR(n1_bit_alu_7_or), .AND(n1_bit_alu_7_and), .NOT(n1_bit_alu_7_not),
    .C_out(n1_bit_alu_7_c_out));
  and and_7 (and_7_out, not_4_out, B[6]);
  _1_Bit_ALU u_1_bit_alu_8 (
    .A1(A[7]), .B1(and_8_out), .Sub(or_2_out), .C_in(n1_bit_alu_7_c_out), .SUM(n1_bit_alu_8_sum),
    .XOR(n1_bit_alu_8_xor), .OR(n1_bit_alu_8_or), .AND(n1_bit_alu_8_and), .NOT(n1_bit_alu_8_not),
    .C_out(C_out));
  and and_8 (and_8_out, not_4_out, B[7]);
  _1_Bit_Multiplexer u_1_bit_multiplexer_1 (
    .O3(O3), .O2(O2), .O1(O1), .NOT(n1_bit_alu_1_not), .AND(n1_bit_alu_1_and), .OR(n1_bit_alu_1_or),
    .XOR(n1_bit_alu_1_xor), .SUM(n1_bit_alu_1_sum), .out_10(Content_Viewer_1[0]), .O4(O4));
  _1_Bit_Multiplexer u_1_bit_multiplexer_2 (
    .O3(O3), .O2(O2), .O1(O1), .NOT(n1_bit_alu_2_not), .AND(n1_bit_alu_2_and), .OR(n1_bit_alu_2_or),
    .XOR(n1_bit_alu_2_xor), .SUM(n1_bit_alu_2_sum), .out_10(Content_Viewer_1[1]), .O4(O4));
  _1_Bit_Multiplexer u_1_bit_multiplexer_3 (
    .O3(O3), .O2(O2), .O1(O1), .NOT(n1_bit_alu_3_not), .AND(n1_bit_alu_3_and), .OR(n1_bit_alu_3_or),
    .XOR(n1_bit_alu_3_xor), .SUM(n1_bit_alu_3_sum), .out_10(Content_Viewer_1[2]), .O4(O4));
  _1_Bit_Multiplexer u_1_bit_multiplexer_4 (
    .O3(O3), .O2(O2), .O1(O1), .NOT(n1_bit_alu_4_not), .AND(n1_bit_alu_4_and), .OR(n1_bit_alu_4_or),
    .XOR(n1_bit_alu_4_xor), .SUM(n1_bit_alu_4_sum), .out_10(Content_Viewer_1[3]), .O4(O4));
  _1_Bit_Multiplexer u_1_bit_multiplexer_5 (
    .O3(O3), .O2(O2), .O1(O1), .NOT(n1_bit_alu_5_not), .AND(n1_bit_alu_5_and), .OR(n1_bit_alu_5_or),
    .XOR(n1_bit_alu_5_xor), .SUM(n1_bit_alu_5_sum), .out_10(Content_Viewer_1[4]), .O4(O4));
  _1_Bit_Multiplexer u_1_bit_multiplexer_6 (
    .O3(O3), .O2(O2), .O1(O1), .NOT(n1_bit_alu_6_not), .AND(n1_bit_alu_6_and), .OR(n1_bit_alu_6_or),
    .XOR(n1_bit_alu_6_xor), .SUM(n1_bit_alu_6_sum), .out_10(Content_Viewer_1[5]), .O4(O4));
  _1_Bit_Multiplexer u_1_bit_multiplexer_7 (
    .O3(O3), .O2(O2), .O1(O1), .NOT(n1_bit_alu_7_not), .AND(n1_bit_alu_7_and), .OR(n1_bit_alu_7_or),
    .XOR(n1_bit_alu_7_xor), .SUM(n1_bit_alu_7_sum), .out_10(Content_Viewer_1[6]), .O4(O4));
  _1_Bit_Multiplexer u_1_bit_multiplexer_8 (
    .O3(O3), .O2(O2), .O1(O1), .NOT(n1_bit_alu_8_not), .AND(n1_bit_alu_8_and), .OR(n1_bit_alu_8_or),
    .XOR(n1_bit_alu_8_xor), .SUM(n1_bit_alu_8_sum), .out_10(Content_Viewer_1[7]), .O4(O4));
  or OR_4 (OR_4_out, O4, O3, O2, O1);
  or or_5 (or_5_out, Content_Viewer_1[7], Content_Viewer_1[6], Content_Viewer_1[5], Content_Viewer_1[4], Content_Viewer_1[3], Content_Viewer_1[2], Content_Viewer_1[1], Content_Viewer_1[0]);
  not not_11 (is_zero, or_5_out);
  assign OUT[0] = OR_4_out ? Content_Viewer_1[0] : 1'bz;  // Controlled_Buffer controlled_buffer_1
  assign OUT[1] = OR_4_out ? Content_Viewer_1[1] : 1'bz;  // Controlled_Buffer controlled_buffer_2
  assign OUT[2] = OR_4_out ? Content_Viewer_1[2] : 1'bz;  // Controlled_Buffer controlled_buffer_3
  assign OUT[3] = OR_4_out ? Content_Viewer_1[3] : 1'bz;  // Controlled_Buffer controlled_buffer_4
  assign OUT[4] = OR_4_out ? Content_Viewer_1[4] : 1'bz;  // Controlled_Buffer controlled_buffer_5
  assign OUT[5] = OR_4_out ? Content_Viewer_1[5] : 1'bz;  // Controlled_Buffer controlled_buffer_6
  assign OUT[6] = OR_4_out ? Content_Viewer_1[6] : 1'bz;  // Controlled_Buffer controlled_buffer_7
  assign OUT[7] = OR_4_out ? Content_Viewer_1[7] : 1'bz;  // Controlled_Buffer controlled_buffer_8

  assign Content_Viewer_2 = Content_Viewer_1;
  assign Content_Viewer_3 = Content_Viewer_1;
  assign is_neg = Content_Viewer_1[7];

  // Notes on the sheet:
  //   B deaktivieren
  //   SUB
  //   C_in
  //   0000 None
  //   0001 ADD
  //   0010 SUB
  //   0011 AND
  //   0100 OR
  //   0101 NOT
  //   0110 XOR
  //   0111 DEC
  //   1000 INC
  //   1001 AOUT
endmodule

module _16_Bit_ALU (
  input  O4,
  input  O3,
  input  O2,
  input  O1,
  input  [15:0] B1,
  input  [15:0] A1,
  output [15:0] OUT,
  output [15:0] CONTENT_VIEWER_1,
  output [15:0] CONTENT_VIEWER_2,
  output [15:0] CONTENT_VIEWER_3,
  output [15:0] CONTENT_VIEWER_4,
  output NEG,
  output COUT,
  output ZERO,
  output OV
);

  wire and_1_out, and_2_out, and_3_out, and_4_out, and_5_out, and_6_out, and_7_out, and_8_out, and_9_out,
       and_10_out, and_11_out, and_12_out, and_13_out, and_14_out, and_15_out, and_16_out, and_17_out,
       and_18_out, and_19_out, and_20_out, n1_bit_alu_1_c_out, n1_bit_alu_2_c_out, n1_bit_alu_3_c_out,
       n1_bit_alu_4_c_out, n1_bit_alu_5_c_out, n1_bit_alu_6_c_out, n1_bit_alu_7_c_out, n1_bit_alu_8_c_out,
       n1_bit_alu_9_c_out, n1_bit_alu_10_c_out, n1_bit_alu_11_c_out, n1_bit_alu_12_c_out,
       n1_bit_alu_13_c_out, n1_bit_alu_14_c_out, n1_bit_alu_15_c_out, nor_1_out, or_1_out, or_2_out, or_3_out;
  wire [15:0] n1_bit_alu_1_and, n1_bit_alu_1_not, n1_bit_alu_1_or, n1_bit_alu_1_sum, n1_bit_alu_1_xor,
       shifter_1_out, shifter_2_out;

  and and_1 (and_1_out, ~O4, ~O3, O2, ~O1);  // AND_Gate
  nor nor_1 (nor_1_out, and_2_out, and_3_out, and_4_out);
  and and_2 (and_2_out, O4, ~O3, ~O2, ~O1);  // AND_Gate
  and and_3 (and_3_out, ~O4, O3, O2, O1);  // AND_Gate
  or or_1 (or_1_out, and_1_out, and_3_out);
  and and_4 (and_4_out, O4, ~O3, ~O2, O1);  // AND_Gate
  or or_2 (or_2_out, and_1_out, and_2_out);
  _1_Bit_ALU u_1_bit_alu_1 (
    .A1(A1[0]), .B1(and_5_out), .Sub(or_1_out), .C_in(or_2_out), .SUM(n1_bit_alu_1_sum[0]),
    .XOR(n1_bit_alu_1_xor[0]), .OR(n1_bit_alu_1_or[0]), .AND(n1_bit_alu_1_and[0]), .NOT(n1_bit_alu_1_not[0]),
    .C_out(n1_bit_alu_1_c_out));
  and and_5 (and_5_out, nor_1_out, B1[0]);
  _1_Bit_ALU u_1_bit_alu_2 (
    .A1(A1[1]), .B1(and_6_out), .Sub(or_1_out), .C_in(n1_bit_alu_1_c_out), .SUM(n1_bit_alu_1_sum[1]),
    .XOR(n1_bit_alu_1_xor[1]), .OR(n1_bit_alu_1_or[1]), .AND(n1_bit_alu_1_and[1]), .NOT(n1_bit_alu_1_not[1]),
    .C_out(n1_bit_alu_2_c_out));
  and and_6 (and_6_out, nor_1_out, B1[1]);
  _1_Bit_ALU u_1_bit_alu_3 (
    .A1(A1[2]), .B1(and_7_out), .Sub(or_1_out), .C_in(n1_bit_alu_2_c_out), .SUM(n1_bit_alu_1_sum[2]),
    .XOR(n1_bit_alu_1_xor[2]), .OR(n1_bit_alu_1_or[2]), .AND(n1_bit_alu_1_and[2]), .NOT(n1_bit_alu_1_not[2]),
    .C_out(n1_bit_alu_3_c_out));
  and and_7 (and_7_out, nor_1_out, B1[2]);
  _1_Bit_ALU u_1_bit_alu_4 (
    .A1(A1[3]), .B1(and_8_out), .Sub(or_1_out), .C_in(n1_bit_alu_3_c_out), .SUM(n1_bit_alu_1_sum[3]),
    .XOR(n1_bit_alu_1_xor[3]), .OR(n1_bit_alu_1_or[3]), .AND(n1_bit_alu_1_and[3]), .NOT(n1_bit_alu_1_not[3]),
    .C_out(n1_bit_alu_4_c_out));
  and and_8 (and_8_out, nor_1_out, B1[3]);
  _1_Bit_ALU u_1_bit_alu_5 (
    .A1(A1[4]), .B1(and_9_out), .Sub(or_1_out), .C_in(n1_bit_alu_4_c_out), .SUM(n1_bit_alu_1_sum[4]),
    .XOR(n1_bit_alu_1_xor[4]), .OR(n1_bit_alu_1_or[4]), .AND(n1_bit_alu_1_and[4]), .NOT(n1_bit_alu_1_not[4]),
    .C_out(n1_bit_alu_5_c_out));
  and and_9 (and_9_out, nor_1_out, B1[4]);
  _1_Bit_ALU u_1_bit_alu_6 (
    .A1(A1[5]), .B1(and_10_out), .Sub(or_1_out), .C_in(n1_bit_alu_5_c_out), .SUM(n1_bit_alu_1_sum[5]),
    .XOR(n1_bit_alu_1_xor[5]), .OR(n1_bit_alu_1_or[5]), .AND(n1_bit_alu_1_and[5]), .NOT(n1_bit_alu_1_not[5]),
    .C_out(n1_bit_alu_6_c_out));
  and and_10 (and_10_out, nor_1_out, B1[5]);
  _1_Bit_ALU u_1_bit_alu_7 (
    .A1(A1[6]), .B1(and_11_out), .Sub(or_1_out), .C_in(n1_bit_alu_6_c_out), .SUM(n1_bit_alu_1_sum[6]),
    .XOR(n1_bit_alu_1_xor[6]), .OR(n1_bit_alu_1_or[6]), .AND(n1_bit_alu_1_and[6]), .NOT(n1_bit_alu_1_not[6]),
    .C_out(n1_bit_alu_7_c_out));
  and and_11 (and_11_out, nor_1_out, B1[6]);
  _1_Bit_ALU u_1_bit_alu_8 (
    .A1(A1[7]), .B1(and_12_out), .Sub(or_1_out), .C_in(n1_bit_alu_7_c_out), .SUM(n1_bit_alu_1_sum[7]),
    .XOR(n1_bit_alu_1_xor[7]), .OR(n1_bit_alu_1_or[7]), .AND(n1_bit_alu_1_and[7]), .NOT(n1_bit_alu_1_not[7]),
    .C_out(n1_bit_alu_8_c_out));
  and and_12 (and_12_out, nor_1_out, B1[7]);
  _1_Bit_ALU u_1_bit_alu_9 (
    .A1(A1[8]), .B1(and_13_out), .Sub(or_1_out), .C_in(n1_bit_alu_8_c_out), .SUM(n1_bit_alu_1_sum[8]),
    .XOR(n1_bit_alu_1_xor[8]), .OR(n1_bit_alu_1_or[8]), .AND(n1_bit_alu_1_and[8]), .NOT(n1_bit_alu_1_not[8]),
    .C_out(n1_bit_alu_9_c_out));
  and and_13 (and_13_out, nor_1_out, B1[8]);
  _1_Bit_ALU u_1_bit_alu_10 (
    .A1(A1[9]), .B1(and_14_out), .Sub(or_1_out), .C_in(n1_bit_alu_9_c_out), .SUM(n1_bit_alu_1_sum[9]),
    .XOR(n1_bit_alu_1_xor[9]), .OR(n1_bit_alu_1_or[9]), .AND(n1_bit_alu_1_and[9]), .NOT(n1_bit_alu_1_not[9]),
    .C_out(n1_bit_alu_10_c_out));
  and and_14 (and_14_out, nor_1_out, B1[9]);
  _1_Bit_ALU u_1_bit_alu_11 (
    .A1(A1[10]), .B1(and_15_out), .Sub(or_1_out), .C_in(n1_bit_alu_10_c_out), .SUM(n1_bit_alu_1_sum[10]),
    .XOR(n1_bit_alu_1_xor[10]), .OR(n1_bit_alu_1_or[10]), .AND(n1_bit_alu_1_and[10]),
    .NOT(n1_bit_alu_1_not[10]), .C_out(n1_bit_alu_11_c_out));
  and and_15 (and_15_out, nor_1_out, B1[10]);
  _1_Bit_ALU u_1_bit_alu_12 (
    .A1(A1[11]), .B1(and_16_out), .Sub(or_1_out), .C_in(n1_bit_alu_11_c_out), .SUM(n1_bit_alu_1_sum[11]),
    .XOR(n1_bit_alu_1_xor[11]), .OR(n1_bit_alu_1_or[11]), .AND(n1_bit_alu_1_and[11]),
    .NOT(n1_bit_alu_1_not[11]), .C_out(n1_bit_alu_12_c_out));
  and and_16 (and_16_out, nor_1_out, B1[11]);
  _1_Bit_ALU u_1_bit_alu_13 (
    .A1(A1[12]), .B1(and_17_out), .Sub(or_1_out), .C_in(n1_bit_alu_12_c_out), .SUM(n1_bit_alu_1_sum[12]),
    .XOR(n1_bit_alu_1_xor[12]), .OR(n1_bit_alu_1_or[12]), .AND(n1_bit_alu_1_and[12]),
    .NOT(n1_bit_alu_1_not[12]), .C_out(n1_bit_alu_13_c_out));
  and and_17 (and_17_out, nor_1_out, B1[12]);
  _1_Bit_ALU u_1_bit_alu_14 (
    .A1(A1[13]), .B1(and_18_out), .Sub(or_1_out), .C_in(n1_bit_alu_13_c_out), .SUM(n1_bit_alu_1_sum[13]),
    .XOR(n1_bit_alu_1_xor[13]), .OR(n1_bit_alu_1_or[13]), .AND(n1_bit_alu_1_and[13]),
    .NOT(n1_bit_alu_1_not[13]), .C_out(n1_bit_alu_14_c_out));
  and and_18 (and_18_out, nor_1_out, B1[13]);
  _1_Bit_ALU u_1_bit_alu_15 (
    .A1(A1[14]), .B1(and_19_out), .Sub(or_1_out), .C_in(n1_bit_alu_14_c_out), .SUM(n1_bit_alu_1_sum[14]),
    .XOR(n1_bit_alu_1_xor[14]), .OR(n1_bit_alu_1_or[14]), .AND(n1_bit_alu_1_and[14]),
    .NOT(n1_bit_alu_1_not[14]), .C_out(n1_bit_alu_15_c_out));
  and and_19 (and_19_out, nor_1_out, B1[14]);
  _1_Bit_ALU u_1_bit_alu_16 (
    .A1(A1[15]), .B1(and_20_out), .Sub(or_1_out), .C_in(n1_bit_alu_15_c_out), .SUM(n1_bit_alu_1_sum[15]),
    .XOR(n1_bit_alu_1_xor[15]), .OR(n1_bit_alu_1_or[15]), .AND(n1_bit_alu_1_and[15]),
    .NOT(n1_bit_alu_1_not[15]), .C_out(COUT));
  and and_20 (and_20_out, nor_1_out, B1[15]);
  Shifter #(.width(16)) shifter_1 (.in(A1), .\dist (B1[3:0]), .out(shifter_1_out));
  Shifter #(.width(16), .shift("lr")) shifter_2 (.in(A1), .\dist (B1[3:0]), .out(shifter_2_out));
  or or_3 (or_3_out, O4, O3, O2, O1);
  Multiplexer #(.select(4), .width(16), .enable("false")) multiplexer_1 (
    .in0({16{1'b0}}), .in1(n1_bit_alu_1_sum), .in2(n1_bit_alu_1_sum), .in3(n1_bit_alu_1_and),
    .in4(n1_bit_alu_1_or), .in5(n1_bit_alu_1_not), .in6(n1_bit_alu_1_xor), .in7(n1_bit_alu_1_sum),
    .in8(n1_bit_alu_1_sum), .in9(n1_bit_alu_1_sum), .in10(shifter_1_out), .in11(shifter_2_out),
    .out(CONTENT_VIEWER_1), .sel({O4, O3, O2, O1}));  // open: in12, in13, in14, in15
  nor nor_2 (ZERO, CONTENT_VIEWER_1[15], CONTENT_VIEWER_1[14], CONTENT_VIEWER_1[13], CONTENT_VIEWER_1[12], CONTENT_VIEWER_1[11], CONTENT_VIEWER_1[10], CONTENT_VIEWER_1[9], CONTENT_VIEWER_1[8], CONTENT_VIEWER_1[6], CONTENT_VIEWER_1[5], CONTENT_VIEWER_1[4], CONTENT_VIEWER_1[3], CONTENT_VIEWER_1[2], CONTENT_VIEWER_1[1], CONTENT_VIEWER_1[0], CONTENT_VIEWER_1[7]);
  xor xor_1 (OV, n1_bit_alu_15_c_out, COUT);
  assign OUT = or_3_out ? CONTENT_VIEWER_1 : 16'bz;  // Controlled_Buffer controlled_buffer_1

  assign CONTENT_VIEWER_2 = CONTENT_VIEWER_1;
  assign CONTENT_VIEWER_3 = CONTENT_VIEWER_1;
  assign CONTENT_VIEWER_4 = CONTENT_VIEWER_1;
  assign NEG = CONTENT_VIEWER_1[15];

  // Notes on the sheet:
  //   0000 None
  //   0001 ADD
  //   0010 SUB
  //   0011 AND
  //   0100 OR
  //   0101 NOT
  //   0110 XOR
  //   0111 DEC
  //   1000 INC
  //   1001 AOUT
  //   1010 SHIFTL
  //   1011 SHIFTR
  //   SUB
  //   DEACT B
  //   INC
  //   DEC
  //   CIN
  //   SUB
  //   AOUT
  //   NOT
  //   Bit Shifter
  //   AND
  //   OR
  //   XOR
  //   SUM
endmodule

module _8_Byte_RAM (
  input  CLK,
  input  Write,
  input  A2,
  input  A1,
  input  A0,
  input  [7:0] in_6,
  input  in_7,
  output [7:0] out_8
);

  wire and_1_out, and_2_out, and_3_out, and_4_out, and_5_out, and_6_out, and_7_out, and_8_out, and_9_out,
       and_10_out, and_11_out, and_12_out, and_13_out, and_14_out, and_15_out, and_16_out, and_17_out,
       and_18_out, and_19_out, and_20_out, and_21_out, and_22_out, and_23_out, and_24_out, not_1_out,
       not_2_out, not_3_out, not_4_out;
  wire [7:0] n8_bit_register_1_content_viewer_1, n8_bit_register_2_content_viewer_1,
       n8_bit_register_3_content_viewer_1, n8_bit_register_4_content_viewer_1,
       n8_bit_register_5_content_viewer_1, n8_bit_register_6_content_viewer_1,
       n8_bit_register_7_content_viewer_1, n8_bit_register_8_content_viewer_1;

  _8_Bit_Register u_8_bit_register_1 (
    .CLK(CLK), .Enable(and_2_out), .Load(and_1_out), .CLR(in_7), .D(in_6), .OUT(out_8),
    .Content_Viewer_1(n8_bit_register_1_content_viewer_1));  // open: Content_Viewer_2, DIR_OUT
  _8_Bit_Register u_8_bit_register_2 (
    .CLK(CLK), .Enable(and_4_out), .Load(and_3_out), .CLR(in_7), .D(in_6), .OUT(out_8),
    .Content_Viewer_1(n8_bit_register_2_content_viewer_1));  // open: Content_Viewer_2, DIR_OUT
  _8_Bit_Register u_8_bit_register_3 (
    .CLK(CLK), .Enable(and_6_out), .Load(and_5_out), .CLR(in_7), .D(in_6), .OUT(out_8),
    .Content_Viewer_1(n8_bit_register_3_content_viewer_1));  // open: Content_Viewer_2, DIR_OUT
  _8_Bit_Register u_8_bit_register_4 (
    .CLK(CLK), .Enable(and_8_out), .Load(and_7_out), .CLR(in_7), .D(in_6), .OUT(out_8),
    .Content_Viewer_1(n8_bit_register_4_content_viewer_1));  // open: Content_Viewer_2, DIR_OUT
  _8_Bit_Register u_8_bit_register_5 (
    .CLK(CLK), .Enable(and_10_out), .Load(and_9_out), .CLR(in_7), .D(in_6), .OUT(out_8),
    .Content_Viewer_1(n8_bit_register_5_content_viewer_1));  // open: Content_Viewer_2, DIR_OUT
  _8_Bit_Register u_8_bit_register_6 (
    .CLK(CLK), .Enable(and_12_out), .Load(and_11_out), .CLR(in_7), .D(in_6), .OUT(out_8),
    .Content_Viewer_1(n8_bit_register_6_content_viewer_1));  // open: Content_Viewer_2, DIR_OUT
  _8_Bit_Register u_8_bit_register_7 (
    .CLK(CLK), .Enable(and_14_out), .Load(and_13_out), .CLR(in_7), .D(in_6), .OUT(out_8),
    .Content_Viewer_1(n8_bit_register_7_content_viewer_1));  // open: Content_Viewer_2, DIR_OUT
  _8_Bit_Register u_8_bit_register_8 (
    .CLK(CLK), .Enable(and_16_out), .Load(and_15_out), .CLR(in_7), .D(in_6), .OUT(out_8),
    .Content_Viewer_1(n8_bit_register_8_content_viewer_1));  // open: Content_Viewer_2, DIR_OUT
  // Probe on n8_bit_register_1_content_viewer_1
  // Probe on n8_bit_register_2_content_viewer_1
  // Probe on n8_bit_register_3_content_viewer_1
  // Probe on n8_bit_register_4_content_viewer_1
  // Probe on n8_bit_register_5_content_viewer_1
  // Probe on n8_bit_register_6_content_viewer_1
  // Probe on n8_bit_register_7_content_viewer_1
  // Probe on n8_bit_register_8_content_viewer_1
  and and_1 (and_1_out, Write, and_17_out);
  and and_2 (and_2_out, not_1_out, and_17_out);
  and and_3 (and_3_out, Write, and_18_out);
  and and_4 (and_4_out, not_1_out, and_18_out);
  and and_5 (and_5_out, Write, and_19_out);
  and and_6 (and_6_out, not_1_out, and_19_out);
  and and_7 (and_7_out, Write, and_20_out);
  and and_8 (and_8_out, not_1_out, and_20_out);
  and and_9 (and_9_out, Write, and_21_out);
  and and_10 (and_10_out, not_1_out, and_21_out);
  and and_11 (and_11_out, Write, and_22_out);
  and and_12 (and_12_out, not_1_out, and_22_out);
  and and_13 (and_13_out, Write, and_23_out);
  and and_14 (and_14_out, not_1_out, and_23_out);
  and and_15 (and_15_out, Write, and_24_out);
  and and_16 (and_16_out, not_1_out, and_24_out);
  not not_1 (not_1_out, Write);
  not not_2 (not_2_out, A2);
  and and_17 (and_17_out, not_2_out, not_3_out, not_4_out);
  and and_18 (and_18_out, not_2_out, not_3_out, A0);
  and and_19 (and_19_out, not_2_out, A1, not_4_out);
  and and_20 (and_20_out, not_2_out, A1, A0);
  and and_21 (and_21_out, A2, not_3_out, not_4_out);
  and and_22 (and_22_out, A2, not_3_out, A0);
  and and_23 (and_23_out, A2, A1, not_4_out);
  and and_24 (and_24_out, A2, A1, A0);
  not not_3 (not_3_out, A1);
  not not_4 (not_4_out, A0);

  // Notes on the sheet:
  //   Adressbreite: 3 Bit ==> 8 Adressen
  //   Datenwortbreite: 8 Bit (1 Byte)
  //   8 Bit RAM Bus
endmodule

// JK Flipflop
module Master_Slave_JK_Flipflop (
  input  CLR,
  input  S_J,
  input  CLK,
  input  R_K,
  output Q,
  output Q_2
);

  wire and_1_out, and_2_out, and_3_out, and_4_out, NOR_2_out, NOR_out, not_1_out, OR_out;

  and and_1 (and_1_out, Q_2, S_J, CLK);
  and and_2 (and_2_out, CLK, R_K, Q);
  or OR (OR_out, CLR, and_2_out);
  and and_3 (and_3_out, NOR_out, not_1_out);
  nor NOR (NOR_out, and_1_out, NOR_2_out);
  nor NOR_2 (NOR_2_out, NOR_out, OR_out);
  and and_4 (and_4_out, not_1_out, NOR_2_out);
  not not_1 (not_1_out, CLK);
  nor NOR_3 (Q, and_3_out, Q_2);
  nor NOR_4 (Q_2, Q, and_4_out);
endmodule

// Pointer
module _1_Bit_Pointer (
  input  IP,
  input  C_in,
  input  LP,
  input  D,
  input  CLK,
  input  CLR,
  output O
);

  wire and_1_out, and_2_out, and_3_out, and_4_out, not_1_out, or_1_out, or_2_out, or_3_out;

  and and_1 (and_1_out, D, LP);
  and and_2 (and_2_out, LP, not_1_out);
  not not_1 (not_1_out, D);
  and and_3 (and_3_out, C_in, IP);
  and and_4 (and_4_out, LP, CLK);
  or or_1 (or_1_out, and_1_out, IP);
  or or_2 (or_2_out, IP, and_2_out);
  or or_3 (or_3_out, and_3_out, and_4_out);
  J_K_Flip_Flop #(.trigger("falling")) j_k_ff_1 (
    .J(or_1_out), .clk(or_3_out), .K(or_2_out), .Q(O), .reset(CLR));  // open: Qn, preset, en
endmodule

module _8_Bit_Pointer (
  input  EP,
  input  CLK,
  input  CLR,
  input  IP,
  input  LP,
  input  [7:0] D,
  output [7:0] Content_Viewer_1,
  output [7:0] OUT,
  output [7:0] Content_Viewer_1_2,
  output [7:0] Content_Viewer_1_3
);

  wire not_1_out;

  not not_1 (not_1_out, CLK);
  Pull_Resistor pull_resistor_1 (.node(LP));
  Pull_Resistor pull_resistor_2 (.node(IP));
  _1_Bit_Pointer u_1_bit_pointer_1 (
    .C_in(not_1_out), .CLR(CLR), .CLK(not_1_out), .IP(IP), .LP(LP), .D(D[0]), .O(Content_Viewer_1[0]));
  _1_Bit_Pointer u_1_bit_pointer_2 (
    .C_in(Content_Viewer_1[0]), .CLR(CLR), .CLK(not_1_out), .IP(IP), .LP(LP), .D(D[1]),
    .O(Content_Viewer_1[1]));
  _1_Bit_Pointer u_1_bit_pointer_3 (
    .C_in(Content_Viewer_1[1]), .CLR(CLR), .CLK(not_1_out), .IP(IP), .LP(LP), .D(D[2]),
    .O(Content_Viewer_1[2]));
  _1_Bit_Pointer u_1_bit_pointer_4 (
    .C_in(Content_Viewer_1[2]), .CLR(CLR), .CLK(not_1_out), .IP(IP), .LP(LP), .D(D[3]),
    .O(Content_Viewer_1[3]));
  _1_Bit_Pointer u_1_bit_pointer_5 (
    .C_in(Content_Viewer_1[3]), .CLR(CLR), .CLK(not_1_out), .IP(IP), .LP(LP), .D(D[4]),
    .O(Content_Viewer_1[4]));
  _1_Bit_Pointer u_1_bit_pointer_6 (
    .C_in(Content_Viewer_1[4]), .CLR(CLR), .CLK(not_1_out), .IP(IP), .LP(LP), .D(D[5]),
    .O(Content_Viewer_1[5]));
  _1_Bit_Pointer u_1_bit_pointer_7 (
    .C_in(Content_Viewer_1[5]), .CLR(CLR), .CLK(not_1_out), .IP(IP), .LP(LP), .D(D[6]),
    .O(Content_Viewer_1[6]));
  _1_Bit_Pointer u_1_bit_pointer_8 (
    .C_in(Content_Viewer_1[6]), .CLR(CLR), .CLK(not_1_out), .IP(IP), .LP(LP), .D(D[7]),
    .O(Content_Viewer_1[7]));
  Pull_Resistor pull_resistor_3 (.node(EP));
  assign OUT[0] = EP ? Content_Viewer_1[0] : 1'bz;  // Controlled_Buffer controlled_buffer_1
  assign OUT[1] = EP ? Content_Viewer_1[1] : 1'bz;  // Controlled_Buffer controlled_buffer_2
  assign OUT[2] = EP ? Content_Viewer_1[2] : 1'bz;  // Controlled_Buffer controlled_buffer_3
  assign OUT[3] = EP ? Content_Viewer_1[3] : 1'bz;  // Controlled_Buffer controlled_buffer_4
  assign OUT[4] = EP ? Content_Viewer_1[4] : 1'bz;  // Controlled_Buffer controlled_buffer_5
  assign OUT[5] = EP ? Content_Viewer_1[5] : 1'bz;  // Controlled_Buffer controlled_buffer_6
  assign OUT[6] = EP ? Content_Viewer_1[6] : 1'bz;  // Controlled_Buffer controlled_buffer_7
  assign OUT[7] = EP ? Content_Viewer_1[7] : 1'bz;  // Controlled_Buffer controlled_buffer_8

  assign Content_Viewer_1_2 = Content_Viewer_1;
  assign Content_Viewer_1_3 = Content_Viewer_1;
endmodule

module _8_Bit_Pointer_2 (
  input  EP,
  input  LP,
  input  IP,
  input  CLK,
  input  CLR,
  input  [7:0] D,
  output [7:0] OUT,
  output [7:0] Content_Viewer_1,
  output [7:0] Content_Viewer_1_2,
  output [7:0] Content_Viewer_1_3
);

  Counter counter_1 (.load(LP), .D(D), .count(IP), .Q(Content_Viewer_1), .clk(CLK), .clr(CLR));  // open: carry
  assign OUT = EP ? Content_Viewer_1 : 8'bz;  // Controlled_Buffer controlled_buffer_1

  assign Content_Viewer_1_2 = Content_Viewer_1;
  assign Content_Viewer_1_3 = Content_Viewer_1;

  // Notes on the sheet:
  //   Pointer von Logisim
endmodule

module _16_Bit_Pointer (
  input  EP,
  input  LP,
  input  IP,
  input  CLK,
  input  CLR,
  input  [15:0] D,
  output [15:0] OUT,
  output [15:0] Content_Viewer_1,
  output [15:0] Content_Viewer_1_2,
  output [15:0] Content_Viewer_1_3
);

  Counter #(.width(16), .max('hffff)) counter_1 (
    .load(LP), .D(D), .count(IP), .Q(Content_Viewer_1), .clk(CLK), .clr(CLR));  // open: carry
  assign OUT = EP ? Content_Viewer_1 : 16'bz;  // Controlled_Buffer controlled_buffer_1

  assign Content_Viewer_1_2 = Content_Viewer_1;
  assign Content_Viewer_1_3 = Content_Viewer_1;

  // Notes on the sheet:
  //   Pointer von Logisim
endmodule

module \_3_Bit_Zähler  (
  input  CLR,
  input  CLK,
  output [2:0] OUT,
  output [2:0] Content_Viewer
);

  wire not_1_out, or_1_out;

  or or_1 (or_1_out, CLR, CLK);
  Master_Slave_JK_Flipflop master_slave_jk_flipflop_1 (
    .S_J(1'b1), .CLK(not_1_out), .R_K(1'b1), .CLR(CLR), .Q(Content_Viewer[0]));  // open: Q_2
  not not_1 (not_1_out, or_1_out);
  Master_Slave_JK_Flipflop master_slave_jk_flipflop_2 (
    .S_J(1'b1), .CLK(Content_Viewer[0]), .R_K(1'b1), .CLR(CLR), .Q(Content_Viewer[1]));  // open: Q_2
  Master_Slave_JK_Flipflop master_slave_jk_flipflop_3 (
    .S_J(1'b1), .CLK(Content_Viewer[1]), .R_K(1'b1), .CLR(CLR), .Q(Content_Viewer[2]));  // open: Q_2

  assign OUT = Content_Viewer;
endmodule

module _16_Bit_IO_Controller (
  input  [15:0] D_IN,
  input  [15:0] CPU_IN,
  input  L_IOMAR,
  input  W_IO,
  input  R_IO,
  input  [7:0] IE,
  input  DR_0,
  input  DR_1,
  input  CLK,
  input  DR_2,
  input  DR_3,
  input  DR_4,
  input  DR_5,
  input  DR_6,
  input  DR_7,
  output [15:0] CPU_OUT,
  output [15:0] D_OUT,
  output [15:0] Address,
  output CS_0,
  output CS_1,
  output CS_2,
  output CS_3,
  output CS_4,
  output CS_5,
  output CS_6,
  output CS_7,
  output [7:0] IFG,
  output IR
);

  wire or_1_out;
  wire [15:0] controlled_buffer_2_out;

  assign CPU_OUT = R_IO ? controlled_buffer_2_out : 16'bz;  // Controlled_Buffer controlled_buffer_1
  assign controlled_buffer_2_out = or_1_out ? CPU_IN : 16'bz;  // Controlled_Buffer controlled_buffer_2
  or or_1 (or_1_out, L_IOMAR, W_IO);
  Pull_Resistor pull_resistor_1 (.node(L_IOMAR));
  Pull_Resistor pull_resistor_2 (.node(W_IO));
  Pull_Resistor pull_resistor_3 (.node(R_IO));

  // Notes on the sheet:
  //   BiDir Data Bus from CPU
endmodule
